# Fritzing sketch Seatalk 1 PerfBoard sch-v1 (saved by Fritzing 0.9.10b)
stripboards: 1

parts:
  R1 = Resistor [tolerance=±5% power=0.25 resistance=4.7k package=THT]
  R2 = Resistor [tolerance=±5% power=0.25 resistance=39k package=THT]
  R3 = Resistor [tolerance=±5% power=0.25 resistance=15k package=THT]
  R4 = Resistor [tolerance=±5% power=0.25 resistance=27k package=THT]
  R5 = Resistor [tolerance=±5% power=0.25 resistance=6.8k package=THT]
  R6 = Resistor [tolerance=±5% power=0.25 resistance=1k package=THT]
  R7 = Resistor [tolerance=±5% power=0.25 resistance=1k package=THT]
  R8 = Resistor [tolerance=±5% power=0.25 resistance=10 package=THT]
  D1 = Rectifier Diode [part_number=1N4148 package="300 mil [THT]"]
  R9 = Resistor [tolerance=±5% power=0.25 resistance=390 package=THT]
  R10 = Resistor [tolerance=±5% power=0.25 resistance=39k package=THT]
  R11 = Resistor [tolerance=±5% power=0.25 resistance=2.2k package=THT]
  R12 = Resistor [tolerance=±5% power=0.25 resistance=2.2k package=THT]
  R13 = Resistor [tolerance=±5% power=0.25 resistance=10k package=THT]
  R15 = Resistor [tolerance=±5% power=0.25 resistance=2.2k package=THT]
  R16 = Resistor [tolerance=±5% power=0.25 resistance=2.2k package=THT]
  R17 = Resistor [tolerance=±5% power=0.25 resistance=4.7k package=THT]
  D2 = Rectifier Diode [part_number=1N4148 package="300 mil [THT]"]
  L1 = Inductor [inductance=1µH package="400 mil [THT]"]
  L2 = Inductor [inductance=10µH package="400 mil [THT]"]
  L3 = Inductor [inductance=10µH package="400 mil [THT]"]
  L4 = Inductor [inductance=10µH package="400 mil [THT]"]
  C3 = Ceramic Capacitor [capacitance=1µF voltage=35V package="100 mil [THT, multilayer]"]
  C4 = Ceramic Capacitor [capacitance=1µF voltage=35V package="100 mil [THT, multilayer]"]
  D3 = Rectifier Diode [part_number=1N4001 package="300 mil [THT]"]
  D4 = Rectifier Diode [part_number=1N4001 package="300 mil [THT]"]
  R18 = Resistor [tolerance=±5% power=0.25 resistance=10 package=THT]
  R19 = Resistor [tolerance=±5% power=0.25 resistance=10 package=THT]
  U1 = Voltage Regulator - 5V [package="TO220 [THT]"]
  M1 = DOIT Esp32 DevKit v1 (30 pins long, 11 pins width) [part_number=ESP32S-PIN30]
  R20 = Resistor [tolerance=±5% power=0.25 resistance=220 package=THT]
  R21 = Resistor [tolerance=±5% power=0.25 resistance=220 package=THT]
  S3 = Pushbutton [package="[THT]"]
  S1 = Pushbutton [package="[THT]"]
  S2 = Pushbutton [package="[THT]"]
  R22 = Resistor [tolerance=±5% power=0.25 resistance=220 package=THT]
  R23 = Resistor [tolerance=±5% power=0.25 resistance=220 package=THT]
  R24 = Resistor [tolerance=±5% power=0.25 resistance=220 package=THT]
  R14 = Resistor [tolerance=±5% power=0.25 resistance=220 package=THT]
  Q1 = NPN-Transistor Top View [package="TO92 [THT] Top"]
  Q2 = NPN-Transistor Top View [package="TO92 [THT] Top"]
  Q3 = NPN-Transistor Top View [package="TO92 [THT] Top"]
  Q4 = NPN-Transistor Top View [package="TO92 [THT] Top"]
  Q5 = PNP-Transistor Top View [package="TO92 [THT] Top"]
  Q6 = NPN-Transistor Top View [package="TO92 [THT] Top"]
  C7 = Ceramic Capacitor [capacitance="100 nF" voltage=35V package="0603 [SMD, multilayer]"]
  C2 = Ceramic Capacitor top view [package="200 mil"]
  C10_-_330uF = Electrolytic Capacitor top view [package="100 mil [THT, electrolytic]"]
  C11_-_220uF = Electrolytic Capacitor top view [package="100 mil [THT, electrolytic]"]
  J1 = screw terminal, 5 pins
  LED3 = LED Red 3mm - Top [color="Red (633nm)" package="3 mm [THT] Top"]
  LED4 = LED Red 3mm - Top [color="Red (633nm)" package="3 mm [THT] Top"]

nets:
  N1: R1.Pin_0, R2.Pin_0, Q1.B
  GND: R1.Pin_1, R8.Pin_0, L4.pin_1, C4.0, U1.GND, M1.GND, S3.Pin_1, S3.Pin_2, S1.Pin_1, S1.Pin_2, S2.Pin_1, S2.Pin_2, Q1.E, Q2.E, Q4.E, Q6.E, C7.0, C10_-_330uF.-, C11_-_220uF.-
  N2: R2.Pin_1, R3.Pin_1, D2.anode
  12V: R3.Pin_0, R10.Pin_1, R12.Pin_1, D4.cathode, R14.Pin_1, Q5.E
  N3: R4.Pin_0, Q1.C, Q2.B
  3.3V: R4.Pin_1, R5.Pin_1, R11.Pin_1, R17.Pin_1, M1.3V3, R22.Pin_1, R23.Pin_1, R24.Pin_1, LED3.anode, LED4.anode
  N4: R5.Pin_0, R6.Pin_0, Q2.C
  RXD: R6.Pin_1, M1.D27, M1.D14
  N5: R7.Pin_0, R8.Pin_1, Q3.E
  N6: R7.Pin_1, R16.Pin_0, Q4.B
  N7: D1.cathode, Q3.C
  N8: D1.anode, R9.Pin_0, D2.cathode, L2.pin_1
  N9: R9.Pin_1, R10.Pin_0, Q5.C
  N10: R11.Pin_0, Q3.B, Q4.C
  N11: R12.Pin_0, R13.Pin_1, Q5.B
  N12: R13.Pin_0, C2.1
  N13: R15.Pin_0, Q6.B
  TXD: R15.Pin_1, R16.Pin_1, R17.Pin_0, M1.D12
  Seatalk: L1.pin_0, J1.pin3
  N14: L1.pin_1, L2.pin_0, C7.1
  ST12V: L3.pin_0, C3.1, J1.pin1
  N15: L3.pin_1, C4.1, D3.anode, D4.anode
  ST0V: L4.pin_0, C3.0, J1.pin5
  N16: D3.cathode, R18.Pin_1, R19.Pin_1
  N17: R18.Pin_0, R19.Pin_0, U1.input_voltage, C10_-_330uF.+
  5V: U1.output_voltage, M1.VIN, C11_-_220uF.+
  N18: M1.D5, S1.Pin_3, S1.Pin_4, R24.Pin_0
  N19: M1.D18, S2.Pin_3, S2.Pin_4, R22.Pin_0
  N20: M1.D19, S3.Pin_3, S3.Pin_4, R23.Pin_0
  N21: M1.D25, R20.Pin_0
  N22: M1.D26, R21.Pin_0
  N23: R20.Pin_1, LED3.cathode
  N24: R21.Pin_1, LED4.cathode
  N25: R14.Pin_0, Q6.C, C2.0

notes:
  Raymarine Seatalk 1

custom parts:
  DOIT Esp32 DevKit v1 (30 pins long, 11 pins width): The DOIT Esp32 DevKit v1 is one of the development board created by DOIT to evaluate the ESP-WROOM-32 module. It is based on the ESP32 microcontroller that boasts Wifi, Bluetooth, Ethernet and Low Power support all in a single chip. (vanepp) made breadboard work, adjusted pin numbering and labels and reduced size of schematic and cleaned up pcb. This chip is 30pins long (2 x15) and 11 pins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
  NPN-Transistor Top View: A standard NPN-transistor
  PNP-Transistor Top View: A standard PNP-transistor
  Ceramic Capacitor top view: 100 nF multilayer Ceramic Capacitor breadboard set to top view for perfboard use.
  Electrolytic Capacitor top view: A small electrolytic capacitor breadboard top view for use on perf board
  LED Red 3mm - Top: A generic red LED (~1.8V)
